# Fritzing sketch Projeto (saved by Fritzing 0.9.3b)
breadboards: 1

parts:
  U1 = NodeMCU V3.0
  U3 = 2-Channel 5v Relay Shield [package=relay-2ch5v10a]
  F1 = Fan - Ventilador [package=THT]
  12V = 9V Battery
  DHT1 = DHT11 Humitidy and Temperature Sensor
  Mic1 = KY-038
  Componente1 = RFID-RC522-v3

nets:
  N1: U1.D0, U3.IN1
  N2: U1.D1, DHT1.DATA
  N3: U1.D2, Mic1.pin4
  N4: U1.D3, Componente1.RST
  3V3: U1.3V3, DHT1.VDD, Mic1.pin3, Componente1.3.3V
  GND: U1.GND, U3.GND, DHT1.GND, Mic1.pin2, Componente1.GND
  N5: U1.D5, Componente1.SCK
  N6: U1.D6, Componente1.MISO
  N7: U1.D7, Componente1.MOSI
  N8: U1.VU, U3.VCC
  N9: U3.K1-In, 12V.+
  N10: U3.K1-On, F1.5V
  N11: F1.GND, 12V.-

custom parts:
  NodeMCU V3.0: ESP8266 based NodeMCU
  2-Channel 5v Relay Shield: 2 Channel 5v Relay Shield w. 2x SPD-06VDC-SD-C
  Fan - Ventilador: Ventilador de 2 pines, se encuentra comunmente en computadoras de escritorio
  9V Battery: A nine volt battery
  DHT11 Humitidy and Temperature Sensor: DHT11 Humidity and Temperature Sensor
  KY-038: ky-038 Microphone sound sensor module
  RFID-RC522-v3: A simple China made RFID-RC522 Reader (6x4 cm); do check the pin labels, as this is a MFRC522 based clone.
